// Logisim project seq_circuit.circ as structural Verilog: 1 circuit, main circuit main
module main (
  input  X,
  input  Y,
  output S,
  output Q
);

  wire and_1_out, and_2_out, clock_1_out, or_1_out, xor_1_out;

  xor xor_1 (xor_1_out, X, Y);
  and and_1 (and_1_out, X, Y);
  and and_2 (and_2_out, xor_1_out, Q);
  xor xor_2 (S, xor_1_out, Q);
  Clock clock_1 (.out(clock_1_out));
  D_Flip_Flop d_ff_1 (.clk(clock_1_out), .D(or_1_out), .Q(Q));  // open: Qn, preset, reset
  or or_1 (or_1_out, and_2_out, and_1_out);

  // Notes on the sheet:
  //   C
endmodule
